// Digital circuit MMP-1.dig as structural Verilog
module MMP_1 (
);

  wire Addr_Dest, Addr_Src, Addr_Step, and_1_out, and_2_out, and_3_out, and_4_out, Clk, comparator_1_eq,
       comparator_2_eq, comparator_2_gt, comparator_2_lt, counter_1_ovf, nClk, not_2_out, nReset, or_2_out,
       Out_Dev, Res_out, Reset, Step_Inc;
  wire [1:0] counter_2_out;
  wire [10:0] Addr_Match_out;
  wire [15:0] Addr, Dest, driver_4_out, PrgmStep, Src;
  wire [31:0] Temp_q;
  wire [31:16] driver_4_out_2;

  Button u_Clk (.out(Clk));
  not not_1 (nClk, Clk);
  Button Res (.out(Res_out));
  RS_FF_AS rs_ff_as_1 (.S(Res_out), .R(counter_1_ovf), .Q(Reset), .nQ(nReset));
  Register #(.Bits(16)) u_Src (.D(driver_4_out_2), .C(Clk), .en(Addr_Step), .Q(Src));
  Register #(.Bits(16)) u_Dest (.D(driver_4_out), .C(Clk), .en(Addr_Step), .Q(Dest));
  not not_2 (not_2_out, comparator_1_eq);
  and and_1 (and_1_out, not_2_out, Step_Inc);
  // Probe Clk on Clk
  assign Addr = Addr_Src ? Src : 16'bz;  // Driver driver_1
  assign Addr = Addr_Dest ? Dest : 16'bz;  // Driver driver_2
  Comparator #(.Bits(16)) comparator_1 (.a({16{1'b1}}), .b(Dest), .eq(comparator_1_eq));  // open: gt, lt
  CounterPreset #(.Bits(16)) Step (
    .en(and_1_out), .C(Clk), .dir(1'b0), .in({16{1'b0}}), .ld(1'b0), .clr(Reset), .out(PrgmStep));  // open: ovf
  // Probe Reset on Reset
  Counter #(.Bits(2)) counter_1 (.en(Reset), .C(nClk), .clr(1'b0), .ovf(counter_1_ovf));  // open: out
  assign Addr = Addr_Step ? PrgmStep : 16'bz;  // Driver driver_3
  Register #(.Bits(32)) Temp (.D({driver_4_out_2, driver_4_out}), .C(Clk), .en(Addr_Src), .Q(Temp_q));
  Counter #(.Bits(2)) counter_2 (.en(1'b1), .C(nClk), .clr(Reset), .out(counter_2_out));  // open: ovf
  assign {driver_4_out_2, driver_4_out} = Addr_Dest ? Temp_q : 32'bz;  // Driver driver_4
  // Probe Copy Step on counter_2_out
  Decoder #(.Selector_Bits(2)) decoder_1 (
    .sel(counter_2_out), .out_0(Addr_Step), .out_1(Addr_Src), .out_2(Addr_Dest), .out_3(Step_Inc));
  Comparator #(.Bits(16)) comparator_2 (
    .a(Addr), .b(16'h4000), .gt(comparator_2_gt), .eq(comparator_2_eq), .lt(comparator_2_lt));
  or or_1 (Out_Dev, Addr_Src, Addr_Step);
  LookUpTable #(.Bits(11)) Addr_Match (
    .in0(Addr[0]), .in1(Addr[1]), .in2(Addr[2]), .in3(Addr[3]), .in4(Addr[4]), .in5(Addr[5]), .in6(Addr[6]),
    .in7(Addr[7]), .in8(Addr[8]), .in9(Addr[9]), .in10(Addr[10]), .in11(Addr[11]), .in12(Addr[12]),
    .in13(Addr[13]), .in14(Addr[14]), .in15(Addr[15]), .out(Addr_Match_out));
  and and_2 (and_2_out, comparator_2_lt, Out_Dev);
  and and_3 (and_3_out, Out_Dev, or_2_out);
  or or_2 (or_2_out, comparator_2_gt, comparator_2_eq);
  and and_4 (and_4_out, or_2_out, Addr_Dest);
  // Probe Source on Src
  // Probe Destination on Dest
  ALU alu_1 (
    .Ctrl_In(Addr_Dest), .Ctrl_Out(Out_Dev), .Clk(Clk), .Data_In({driver_4_out_2, driver_4_out}),
    .Sel_A(Addr_Match_out[0]), .Sel_B(Addr_Match_out[1]), .Sel_SUM(Addr_Match_out[2]),
    .Sel_AND(Addr_Match_out[3]), .Sel_OR(Addr_Match_out[4]), .Sel_XOR(Addr_Match_out[5]),
    .Sel_NOT(Addr_Match_out[6]), .Sel_GT(Addr_Match_out[7]), .Sel_GTE(Addr_Match_out[8]),
    .Sel_LT(Addr_Match_out[9]), .Sel_LTE(Addr_Match_out[10]));  // open: Data_Out, Data_Ready
  ROM #(.bigEndian("true"), .AddrBits(14), .Bits(32)) rom_1 (
    .A(Addr[13:0]), .sel(and_2_out), .D({driver_4_out_2, driver_4_out}));
  RAMSinglePortSel #(.AddrBits(14), .Bits(32)) ramsingleportsel_1 (
    .A(Addr[13:0]), .CS(Clk), .WE(and_4_out), .OE(and_3_out), .D({driver_4_out_2, driver_4_out}));
  LED led_1 (.in(Addr_Step));
  LED led_2 (.in(Addr_Src));
  LED led_3 (.in(Addr_Dest));
  LED led_4 (.in(Step_Inc));
  // Probe Program Step on PrgmStep
  // Probe Address on Addr
  // Probe Bus on {driver_4_out_2, driver_4_out}

  // Other names for the same wires on the sheet: MemAddr[13:0] = Addr[13:0]; In_SrcDest = Addr_Step;
  //   In_Temp = Addr_Src; In_Dev = Addr_Dest; Out_Temp = Addr_Dest

  // Notes on the sheet:
  //   contents of Addr_Match (hex, n*v repeats v):
  //   61440*0,1,2,4,8,e,1a,34,80,ae,14a,214
  //   rom_1 loads program.bin
  //   Load pointers
  //   Read Source
  //   Write Destination
  //   Increment Step
  //   0x0000-0x3FFF : ROM
  //   0x4000-0x7FFF : RAM
  //   0xF000-0xF00A : ALU A, B, SUM, AND, OR, XOR, NOT, GT, GTE, LT, LTE
  //   0xFFFF : Step
endmodule
